// Logisim project custom_reg.circ as structural Verilog: 12 circuits, main circuit 1bit_reg
module _1bit_reg (
  input  Clock,
  input  Data,
  input  Clear,
  input  Load,
  output Data_out
);

  wire and_1_out, and_2_out, not_1_out, not_2_out;

  not not_1 (not_1_out, Data);
  and and_1 (and_1_out, Data, Load);
  and and_2 (and_2_out, not_1_out, Load);
  J_K_Flip_Flop j_k_ff_1 (
    .J(and_1_out), .clk(Clock), .K(and_2_out), .Q(Data_out), .preset(1'b0), .en(not_2_out), .reset(Clear));  // open: Qn
  not not_2 (not_2_out, Clear);

  // Notes on the sheet:
  //   Spencer Arnold
  //   OLA 5
  //   RSC Registers
endmodule

// Reg
module Register (
  input  Clock,
  input  [31:0] Data_In,
  input  Load,
  output [31:0] Data_out
);

  Register_part #(.width(32)) register_1 (.D(Data_In), .en(Load), .Q(Data_out), .clk(Clock));  // open: clr
endmodule

// BR
module BusRegister (
  input  Clock,
  input  [31:0] Data_In,
  input  Load,
  input  Bus,
  output [31:0] Data_out,
  output [31:0] Bus_out
);

  Register_part #(.width(32)) register_1 (.D(Data_In), .en(Load), .Q(Data_out), .clk(Clock));  // open: clr
  assign Bus_out = Bus ? Data_out : 32'bz;  // Controlled_Buffer controlled_buffer_1
endmodule

// CR
module ClearRegister (
  input  Clock,
  input  [31:0] Data_In,
  input  Clear,
  input  Load,
  input  Bus,
  output [31:0] Data_out,
  output [31:0] Bus_out
);

  Register_part #(.width(32)) register_1 (.D(Data_In), .en(Load), .Q(Data_out), .clk(Clock), .clr(Clear));
  assign Bus_out = Bus ? Data_out : 32'bz;  // Controlled_Buffer controlled_buffer_1
endmodule

// CTR
module CountRegister (
  input  Clock,
  input  [31:0] Data_In,
  input  Count,
  input  Load,
  input  Bus,
  output [31:0] Data_out,
  output [31:0] Bus_out
);

  wire or_1_out;
  wire [31:0] adder_1_out, multiplexer_1_out;

  Adder #(.width(32)) adder_1 (.a(Data_out), .b({32{1'b0}}), .out(adder_1_out), .cin(Count));  // open: cout
  Multiplexer #(.width(32)) multiplexer_1 (
    .in0(Data_In), .in1(adder_1_out), .out(multiplexer_1_out), .sel(Count));  // open: en
  or or_1 (or_1_out, Count, Load);
  Register_part #(.width(32)) register_1 (
    .D(multiplexer_1_out), .en(or_1_out), .Q(Data_out), .clk(Clock));  // open: clr
  assign Bus_out = Bus ? Data_out : 32'bz;  // Controlled_Buffer controlled_buffer_1
endmodule

module ACC (
  input  Clock,
  input  [31:0] Data_In,
  input  Clear,
  input  Load,
  input  Bus,
  output [31:0] Data_Out,
  output [31:0] Bus_Out
);

  ClearRegister clearregister_1 (
    .Data_In(Data_In), .Clock(Clock), .Clear(Clear), .Load(Load), .Bus(Bus), .Data_out(Data_Out),
    .Bus_out(Bus_Out));
endmodule

module AR (
  input  Clock,
  input  [31:0] Data_In,
  input  Load,
  output [31:0] Data_Out
);

  Register register_1 (.Data_In(Data_In), .Clock(Clock), .Load(Load), .Data_out(Data_Out));
endmodule

module DR (
  input  Clock,
  input  [31:0] Data_In,
  input  Load,
  input  Bus,
  output [31:0] Data_out,
  output [31:0] Bus_out
);

  BusRegister busregister_1 (
    .Data_In(Data_In), .Clock(Clock), .Load(Load), .Bus(Bus), .Data_out(Data_out), .Bus_out(Bus_out));
endmodule

module IR (
  input  Clock,
  input  [31:0] Data_In,
  input  Load,
  output [31:0] Data_out
);

  Register register_1 (.Data_In(Data_In), .Clock(Clock), .Load(Load), .Data_out(Data_out));
endmodule

module OUTR (
  input  Clock,
  input  [31:0] Data_In,
  input  Load,
  output [31:0] Data_out
);

  Register register_1 (.Data_In(Data_In), .Clock(Clock), .Load(Load), .Data_out(Data_out));
endmodule

module PC (
  input  Clock,
  input  [31:0] Data_In,
  input  Count,
  input  Load,
  input  Bus,
  output [31:0] Data_out,
  output [31:0] Bus_out
);

  CountRegister countregister_1 (
    .Data_In(Data_In), .Clock(Clock), .Count(Count), .Load(Load), .Bus(Bus), .Data_out(Data_out),
    .Bus_out(Bus_out));
endmodule

module R (
  input  Clock,
  input  [31:0] Data_In,
  input  Load,
  input  Bus,
  output [31:0] Data_out,
  output [31:0] Bus_out
);

  BusRegister busregister_1 (
    .Data_In(Data_In), .Clock(Clock), .Load(Load), .Bus(Bus), .Data_out(Data_out), .Bus_out(Bus_out));
endmodule
